# Fritzing sketch NanoBotArduino (saved by Fritzing 0.9.4)

parts:
  Componente1 = Arduino Uno (Rev3) - ICSP
  Raspberry_Pi_1 = Raspberry Pi 3 [part_number=RPI-3-V1.2]  # not connected
  Componente2 = Arduino Motor Shield
  M1 = DC Motor
  M2 = DC Motor
  hc-sr1 = hc-sr04
  LED1 = LED - 3mm [color="Red (633nm)" package="3 mm [THT]"]
  R1 = Resistor [tolerance=±5% resistance=220 package="2010 [SMD]"]
  U1 = LIPO-1000mAh [package=lipo-1000]  # not connected
  U2 = LIPO-1000mAh [package=lipo-1000]

nets:
  GND: Componente1.GND, Componente2.GND, hc-sr1.GND, LED1.cathode, U2.-
  N1: Componente1.D10_PWM/SS, Componente2.D10, R1.Pin_1
  N2: Componente1.D11_PWM/MOSI, Componente2.D11
  N3: Componente1.D12/MISO, Componente2.D12
  N4: Componente1.D13/SCK, Componente2.D13
  N5: Componente1.D3_PWM, Componente2.D3
  N6: Componente1.D4, Componente2.D4, hc-sr1.Echo
  N7: Componente1.D5_PWM, Componente2.D5, hc-sr1.Trig
  5V: Componente1.5V, Componente2.5V, hc-sr1.VCC
  N8: Componente2.VIN, U2.+
  N9: Componente2.OUT3, M1.pin_2
  N10: Componente2.OUT4, M1.pin_1
  N11: Componente2.OUT2, M2.pin_1
  N12: Componente2.OUT1, M2.pin_2
